// Logisim project cpu.circ as structural Verilog: 14 circuits, main circuit main
module main (
  input  [7:0] Data_in,
  input  [7:0] Address_Entry,
  input  Memory_Op,
  input  Run,
  output out_5
);

  wire A_enable, B_enable, C_enable, C_in, Clock, decoder_1_out0, decoder_1_out1, decoder_1_out2,
       decoder_1_out3, decoder_1_out4, decoder_1_out5, Halt, MAR_enable, MEM, not_1_out, Reset_out;
  wire [1:0] Reg_Func;
  wire [2:0] ALU_Opcode, Decode;
  wire [7:0] A_output, B_output, C_output, controlled_buffer_1_out, Data_in_t, MAR_output, ram_1_dout;

  Button Execute (.out(Clock));
  Button Reset (.out(Reset_out));
  not not_1 (not_1_out, Memory_Op);
  RAM ram_1 (.addr(Address_Entry), .we(Memory_Op), .oe(not_1_out), .clk(Clock), .din(Data_in_t), .dout(ram_1_dout));
  MicroSeq microseq_1 (
    .Reset(Reset_out), .Clock(Clock), .Run(Run), .Mem(MEM), .Mar(MAR_enable), .C(C_enable), .B(B_enable),
    .A(A_enable), .Data_Source(Decode), .ALU_Function(ALU_Opcode), .C_in(C_in), .Register_Function(Reg_Func),
    .Halt(Halt));
  Decoder #(.select(3)) decoder_1 (
    .out0(decoder_1_out0), .out1(decoder_1_out1), .out2(decoder_1_out2), .out3(decoder_1_out3),
    .out4(decoder_1_out4), .out5(decoder_1_out5), .sel(Decode), .en(1'b1));  // open: out6, out7
  // Probe on Decode
  assign controlled_buffer_1_out = decoder_1_out0 ? Data_in : 8'bz;  // Controlled_Buffer controlled_buffer_1
  assign controlled_buffer_1_out = decoder_1_out1 ? ram_1_dout : 8'bz;  // Controlled_Buffer controlled_buffer_2
  assign controlled_buffer_1_out = decoder_1_out2 ? A_output : 8'bz;  // Controlled_Buffer controlled_buffer_3
  assign controlled_buffer_1_out = decoder_1_out3 ? B_output : 8'bz;  // Controlled_Buffer controlled_buffer_4
  assign controlled_buffer_1_out = decoder_1_out4 ? C_output : 8'bz;  // Controlled_Buffer controlled_buffer_5
  assign controlled_buffer_1_out = decoder_1_out5 ? MAR_output : 8'bz;  // Controlled_Buffer controlled_buffer_6
  ALU8 alu8_1 (
    .in_1(A_output), .in_2(controlled_buffer_1_out), .Cin(C_in), .Opcode(ALU_Opcode),
    ._8_bit_output(Data_in_t), .C_out(out_5));
  Register_Plus A (
    .Clock_Input(Clock), .Select_Line(A_enable), .Function_Line(Reg_Func), .Data(Data_in_t),
    .Register_Output(A_output));  // open: C_out
  // Probe on A_output
  Register_Plus B (
    .Clock_Input(Clock), .Select_Line(B_enable), .Function_Line(Reg_Func), .Data(Data_in_t),
    .Register_Output(B_output));  // open: C_out
  // Probe on B_output
  Register_Plus C (
    .Clock_Input(Clock), .Select_Line(C_enable), .Function_Line(Reg_Func), .Data(Data_in_t),
    .Register_Output(C_output));  // open: C_out
  // Probe on C_output
  Register_Plus MAR (
    .Clock_Input(Clock), .Select_Line(MAR_enable), .Function_Line(Reg_Func), .Data(Data_in_t),
    .Register_Output(MAR_output));  // open: C_out
  // Probe on MAR_output
endmodule

module Register1 (
  input  [7:0] in_1,
  input  Enable,
  output [7:0] Output
);

  wire button_1_out, button_2_out;

  Button button_1 (.out(button_1_out));
  Button button_2 (.out(button_2_out));
  Register register_1 (.D(in_1), .en(Enable), .clk(button_1_out), .Q(Output), .clr(button_2_out));

  // Notes on the sheet:
  //   Input
  //   Clock
  //   Clear
endmodule

module Counter1 (
  input  Load,
  input  Count,
  input  in_3,
  input  [7:0] in_4,
  output C_out,
  output [7:0] out_6
);

  wire button_1_out, button_2_out;

  Button button_1 (.out(button_1_out));
  Counter counter_1 (
    .clr(button_2_out), .load(Load), .up(Count), .count(in_3), .clk(button_1_out), .D(in_4), .carry(C_out),
    .Q(out_6));
  Button button_2 (.out(button_2_out));

  // Notes on the sheet:
  //   Increment-Decrement
  //   Execute
  //   Data Entry
  //   Clear
  //   Counter Output
endmodule

module Register_Plus (
  input  Clock_Input,
  input  Select_Line,
  input  [1:0] Function_Line,
  input  [7:0] Data,
  output C_out,
  output [7:0] Register_Output
);

  wire and_1_out, decoder_1_out0, decoder_1_out1, decoder_1_out2, or_1_out;

  Decoder #(.select(2)) decoder_1 (
    .out0(decoder_1_out0), .out1(decoder_1_out1), .out2(decoder_1_out2), .sel(Function_Line), .en(Select_Line));  // open: out3
  and and_1 (and_1_out, Clock_Input, decoder_1_out1);
  or or_1 (or_1_out, decoder_1_out0, decoder_1_out1);
  Counter counter_1 (
    .clr(and_1_out), .load(or_1_out), .up(decoder_1_out2), .count(Select_Line), .clk(Clock_Input), .D(Data),
    .carry(C_out), .Q(Register_Output));

  // Notes on the sheet:
  //   00 = Load
  //   01 = Clear
  //   10 = Increment
  //   11 = Decrement
endmodule

module MicroSeq (
  input  Reset,
  input  Clock,
  input  Run,
  output Mem,
  output Mar,
  output C,
  output B,
  output A,
  output [2:0] Data_Source,
  output [2:0] ALU_Function,
  output C_in,
  output [1:0] Register_Function,
  output Halt
);

  wire and_1_out, not_1_out;
  wire [7:0] counter_1_q;
  wire [31:15] rom_1_data;

  and and_1 (and_1_out, Clock, Run, not_1_out);
  Counter counter_1 (
    .clr(Reset), .count(1'b1), .clk(and_1_out), .D(rom_1_data[31:24]), .Q(counter_1_q));  // open: load, up, carry
  ROM #(.dataWidth(32)) rom_1 (
    .addr(counter_1_q),
    .data({rom_1_data, Halt, Register_Function, C_in, ALU_Function, Data_Source, A, B, C, Mar, Mem}));
  not not_1 (not_1_out, Halt);

  // Notes on the sheet:
  //   contents of rom_1 (hex, n*v repeats v):
  //   1050 108 104 170 390 4000
endmodule

module Mem (
  input  [7:0] in_1,
  input  [7:0] in_2,
  input  [7:0] in_3,
  input  [7:0] in_4,
  input  Memory_Op,
  input  Memory_Op_2,
  input  [7:0] in_7,
  input  [7:0] in_8,
  input  Memory_Op_3,
  output [7:0] out_10,
  output [7:0] out_11,
  output [7:0] out_12
);

  wire button_1_out, button_2_out, not_1_out, not_2_out;

  Button button_1 (.out(button_1_out));
  RAM #(.databus("bidir")) ram_1 (.addr(in_3), .we(Memory_Op), .oe(not_1_out), .clk(button_1_out), .data(out_10));
  not not_1 (not_1_out, Memory_Op);
  RAM #(.databus("bidir"), .trigger("high")) ram_2 (.addr(in_8), .we(not_2_out), .oe(Memory_Op_3), .data(out_12));
  not not_2 (not_2_out, Memory_Op_3);
  assign out_10 = Memory_Op ? in_1 : 8'bz;  // Controlled_Buffer controlled_buffer_1
  assign out_12 = not_2_out ? in_7 : 8'bz;  // Controlled_Buffer controlled_buffer_2
  Button button_2 (.out(button_2_out));
  RAM ram_3 (.addr(in_4), .we(Memory_Op_2), .oe(Memory_Op_2), .clk(button_2_out), .din(in_2), .dout(out_11));

  // Notes on the sheet:
  //   Data_in
  //   Address_entry
  //   Address_entry
  //   Execute
  //   Data_in
  //   Mode 1
  //   Mode 2
  //   Address_entry
  //   Data_in
  //   Execute
  //   Mode 1 - Separate load/store
endmodule

module Adder1Bit (
  input  A,
  input  B,
  input  C_in,
  output Sum,
  output C_out
);

  wire and_1_out, and_2_out, xor_1_out;

  xor xor_1 (xor_1_out, A, B);
  and and_1 (and_1_out, xor_1_out, C_in);
  and and_2 (and_2_out, A, B);
  xor xor_2 (Sum, xor_1_out, C_in);
  or or_1 (C_out, and_1_out, and_2_out);
endmodule

module Adder4Bit (
  input  [3:0] A,
  input  [3:0] B,
  input  C_in,
  output C_out,
  output [3:0] out_5
);

  wire adder1bit_2_c_out, adder1bit_3_c_out, adder1bit_4_c_out;

  Adder1Bit adder1bit_1 (.A(A[3]), .B(B[3]), .C_in(adder1bit_2_c_out), .C_out(C_out), .Sum(out_5[3]));
  Adder1Bit adder1bit_2 (.A(A[2]), .B(B[2]), .C_in(adder1bit_3_c_out), .C_out(adder1bit_2_c_out), .Sum(out_5[2]));
  Adder1Bit adder1bit_3 (.A(A[1]), .B(B[1]), .C_in(adder1bit_4_c_out), .C_out(adder1bit_3_c_out), .Sum(out_5[1]));
  Adder1Bit adder1bit_4 (.A(A[0]), .B(B[0]), .C_in(C_in), .C_out(adder1bit_4_c_out), .Sum(out_5[0]));

  // Notes on the sheet:
  //   A
  //   Cout
  //   Cout
  //   Cout
  //   B
endmodule

module Adder4Bit1 (
  input  A,
  input  B,
  input  A_2,
  input  B_2,
  input  A_3,
  input  B_3,
  input  A_4,
  input  B_4,
  input  Cout,
  input  Cin,
  output out_11,
  output out_12,
  output out_13,
  output out_14
);

  wire adder1bit_2_c_out, adder1bit_3_c_out, adder1bit_4_c_out;

  Adder1Bit adder1bit_1 (.A(A), .B(B), .C_in(adder1bit_2_c_out), .C_out(Cout), .Sum(out_11));
  Adder1Bit adder1bit_2 (.A(A_2), .B(B_2), .C_in(adder1bit_3_c_out), .C_out(adder1bit_2_c_out), .Sum(out_12));
  Adder1Bit adder1bit_3 (.A(A_3), .B(B_3), .C_in(adder1bit_4_c_out), .C_out(adder1bit_3_c_out), .Sum(out_13));
  Adder1Bit adder1bit_4 (.A(A_4), .B(B_4), .C_in(Cin), .C_out(adder1bit_4_c_out), .Sum(out_14));

  // Notes on the sheet:
  //   Cout
  //   Cout
  //   Cout
endmodule

module Adder8Bit (
  input  [7:0] A,
  input  [7:0] B,
  input  Cin,
  output Cout,
  output [7:0] out_5
);

  wire adder4bit_2_c_out;

  Adder4Bit adder4bit_1 (.A(A[7:4]), .B(B[7:4]), .C_in(adder4bit_2_c_out), .C_out(Cout), .out_5(out_5[7:4]));
  Adder4Bit adder4bit_2 (.A(A[3:0]), .B(B[3:0]), .C_in(Cin), .C_out(adder4bit_2_c_out), .out_5(out_5[3:0]));
endmodule

module ALU8 (
  input  [7:0] in_1,
  input  [7:0] in_2,
  input  Cin,
  input  [2:0] Opcode,
  output [7:0] _8_bit_output,
  output C_out
);

  wire adder8bit_1_cout, comparator_1_eq, comparator_1_lt, decoder_1_out0, decoder_1_out1, decoder_1_out2,
       decoder_1_out3, decoder_1_out4, decoder_1_out5, decoder_1_out6, decoder_1_out7, subtractor_1_bout;
  wire [7:0] adder8bit_1_out_5, and_1_out, bit_extender_1_out, bit_extender_2_out, negator_1_out, not_1_out,
       or_1_out, subtractor_1_out;

  Decoder #(.select(3), .tristate("true")) decoder_1 (
    .out0(decoder_1_out0), .out1(decoder_1_out1), .out2(decoder_1_out2), .out3(decoder_1_out3),
    .out4(decoder_1_out4), .out5(decoder_1_out5), .out6(decoder_1_out6), .out7(decoder_1_out7), .sel(Opcode),
    .en(1'b1));
  Adder8Bit adder8bit_1 (.A(in_1), .B(in_2), .Cin(Cin), .Cout(adder8bit_1_cout), .out_5(adder8bit_1_out_5));
  Subtractor subtractor_1 (.a(in_1), .b(in_2), .out(subtractor_1_out), .bin(Cin), .bout(subtractor_1_bout));
  Negator negator_1 (.in(in_2), .out(negator_1_out));
  Comparator comparator_1 (.a(in_1), .b(in_2), .eq(comparator_1_eq), .lt(comparator_1_lt));  // open: gt
  assign and_1_out = in_1 & in_2;  // AND_Gate and_1, 8 bits wide
  assign _8_bit_output = decoder_1_out0 ? and_1_out : 8'bz;  // Controlled_Buffer controlled_buffer_1
  assign or_1_out = in_1 | in_2;  // OR_Gate or_1, 8 bits wide
  assign not_1_out = ~in_2;  // NOT_Gate not_1, 8 bits wide
  assign C_out = decoder_1_out3 ? adder8bit_1_cout : 1'bz;  // Controlled_Buffer controlled_buffer_2
  assign _8_bit_output = decoder_1_out3 ? adder8bit_1_out_5 : 8'bz;  // Controlled_Buffer controlled_buffer_3
  assign bit_extender_1_out = {{7{comparator_1_eq}}, comparator_1_eq};  // Bit_Extender bit_extender_1
  assign bit_extender_2_out = {{7{comparator_1_lt}}, comparator_1_lt};  // Bit_Extender bit_extender_2
  assign _8_bit_output = decoder_1_out1 ? or_1_out : 8'bz;  // Controlled_Buffer controlled_buffer_4
  assign _8_bit_output = decoder_1_out2 ? not_1_out : 8'bz;  // Controlled_Buffer controlled_buffer_5
  assign _8_bit_output = decoder_1_out5 ? subtractor_1_out : 8'bz;  // Controlled_Buffer controlled_buffer_6
  assign C_out = decoder_1_out5 ? subtractor_1_bout : 1'bz;  // Controlled_Buffer controlled_buffer_7
  assign _8_bit_output = decoder_1_out4 ? negator_1_out : 8'bz;  // Controlled_Buffer controlled_buffer_8
  assign _8_bit_output = decoder_1_out7 ? bit_extender_1_out : 8'bz;  // Controlled_Buffer controlled_buffer_9
  assign _8_bit_output = decoder_1_out6 ? bit_extender_2_out : 8'bz;  // Controlled_Buffer controlled_buffer_10

  // Notes on the sheet:
  //   A
  //   B
  //   B compliment
  //   Adder
  //   Subtractor
  //   B Negation
  //   Comparison
  //   AND
  //   OR
endmodule

module Step3 (
  input  [7:0] in_1,
  input  [7:0] in_2,
  input  Memory_Op,
  input  A,
  input  B,
  input  [1:0] in_6
);

  wire button_1_out, button_2_out, decoder_1_out0, decoder_1_out1, decoder_1_out2, decoder_1_out3, not_1_out;
  wire [7:0] controlled_buffer_1_out, ram_1_dout, register_1_q, register_2_q;

  Button button_1 (.out(button_1_out));
  not not_1 (not_1_out, Memory_Op);
  RAM ram_1 (
    .addr(in_2), .we(Memory_Op), .oe(not_1_out), .clk(button_1_out), .din(controlled_buffer_1_out),
    .dout(ram_1_dout));
  Button button_2 (.out(button_2_out));
  Register register_1 (.D(controlled_buffer_1_out), .en(A), .clk(button_1_out), .Q(register_1_q), .clr(button_2_out));
  Register register_2 (.D(controlled_buffer_1_out), .en(B), .clk(button_1_out), .Q(register_2_q), .clr(button_2_out));
  Decoder #(.select(2)) decoder_1 (
    .out0(decoder_1_out0), .out1(decoder_1_out1), .out2(decoder_1_out2), .out3(decoder_1_out3), .sel(in_6),
    .en(1'b1));
  assign controlled_buffer_1_out = decoder_1_out0 ? in_1 : 8'bz;  // Controlled_Buffer controlled_buffer_1
  assign controlled_buffer_1_out = decoder_1_out1 ? ram_1_dout : 8'bz;  // Controlled_Buffer controlled_buffer_2
  assign controlled_buffer_1_out = decoder_1_out2 ? register_1_q : 8'bz;  // Controlled_Buffer controlled_buffer_3
  assign controlled_buffer_1_out = decoder_1_out3 ? register_2_q : 8'bz;  // Controlled_Buffer controlled_buffer_4

  // Notes on the sheet:
  //   Data_in
  //   Address_entry
  //   Execute
  //   Reset
endmodule

module Step4 (
  input  [7:0] in_1,
  input  [7:0] in_2,
  input  Memory_Op,
  input  C_in,
  input  [2:0] in_5,
  input  A,
  input  B,
  input  [1:0] in_8,
  output [7:0] ALU_output,
  output C_out
);

  wire button_1_out, button_2_out, decoder_1_out0, decoder_1_out1, decoder_1_out2, decoder_1_out3, not_1_out;
  wire [7:0] controlled_buffer_1_out, ram_1_dout, register_1_q, register_2_q;

  Button button_1 (.out(button_1_out));
  not not_1 (not_1_out, Memory_Op);
  RAM ram_1 (.addr(in_2), .we(Memory_Op), .oe(not_1_out), .clk(button_1_out), .din(ALU_output), .dout(ram_1_dout));
  Button button_2 (.out(button_2_out));
  Register register_1 (.D(controlled_buffer_1_out), .en(A), .clk(button_1_out), .Q(register_1_q), .clr(button_2_out));
  Register register_2 (.D(controlled_buffer_1_out), .en(B), .clk(button_1_out), .Q(register_2_q), .clr(button_2_out));
  Decoder #(.select(2)) decoder_1 (
    .out0(decoder_1_out0), .out1(decoder_1_out1), .out2(decoder_1_out2), .out3(decoder_1_out3), .sel(in_8),
    .en(1'b1));
  assign controlled_buffer_1_out = decoder_1_out0 ? in_1 : 8'bz;  // Controlled_Buffer controlled_buffer_1
  assign controlled_buffer_1_out = decoder_1_out1 ? ram_1_dout : 8'bz;  // Controlled_Buffer controlled_buffer_2
  assign controlled_buffer_1_out = decoder_1_out2 ? register_1_q : 8'bz;  // Controlled_Buffer controlled_buffer_3
  assign controlled_buffer_1_out = decoder_1_out3 ? register_2_q : 8'bz;  // Controlled_Buffer controlled_buffer_4
  ALU8 alu8_1 (
    .in_1(register_1_q), .in_2(controlled_buffer_1_out), .Cin(C_in), .Opcode(in_5),
    ._8_bit_output(ALU_output), .C_out(C_out));

  // Notes on the sheet:
  //   Data_in
  //   Address_entry
  //   Execute
  //   Reset
endmodule

module Step5 (
  input  [7:0] in_1,
  input  [7:0] in_2,
  input  Memory_Op,
  input  Cin,
  input  [2:0] in_5,
  input  A,
  input  B,
  input  [1:0] in_8,
  output [7:0] out_9,
  output out_10
);

  wire button_1_out, button_2_out, decoder_1_out0, decoder_1_out1, decoder_1_out2, decoder_1_out3, not_1_out;
  wire [7:0] controlled_buffer_1_out, ram_1_dout, register_1_q, register_2_q;

  Button button_1 (.out(button_1_out));
  not not_1 (not_1_out, Memory_Op);
  RAM ram_1 (
    .addr(in_2), .we(Memory_Op), .oe(not_1_out), .clk(button_1_out), .din(controlled_buffer_1_out),
    .dout(ram_1_dout));
  Button button_2 (.out(button_2_out));
  Register register_1 (.D(controlled_buffer_1_out), .en(A), .clk(button_1_out), .Q(register_1_q), .clr(button_2_out));
  Register register_2 (.D(controlled_buffer_1_out), .en(B), .clk(button_1_out), .Q(register_2_q), .clr(button_2_out));
  Decoder #(.select(2)) decoder_1 (
    .out0(decoder_1_out0), .out1(decoder_1_out1), .out2(decoder_1_out2), .out3(decoder_1_out3), .sel(in_8),
    .en(1'b1));
  assign controlled_buffer_1_out = decoder_1_out0 ? in_1 : 8'bz;  // Controlled_Buffer controlled_buffer_1
  assign controlled_buffer_1_out = decoder_1_out1 ? ram_1_dout : 8'bz;  // Controlled_Buffer controlled_buffer_2
  assign controlled_buffer_1_out = decoder_1_out2 ? register_1_q : 8'bz;  // Controlled_Buffer controlled_buffer_3
  assign controlled_buffer_1_out = decoder_1_out3 ? register_2_q : 8'bz;  // Controlled_Buffer controlled_buffer_4
  ALU8 alu8_1 (
    .in_1(register_1_q), .in_2(controlled_buffer_1_out), .Cin(Cin), .Opcode(in_5), ._8_bit_output(out_9),
    .C_out(out_10));

  // Notes on the sheet:
  //   Data_in
  //   Address_entry
  //   Execute
  //   Reset
  //   A
  //   B
  //   ALU Opcode
endmodule
