// Logisim project gates_circuits.circ as structural Verilog: 5 circuits, main circuit main
module main (
  input  in_1,
  input  [3:0] in_2,
  input  [3:0] in_3,
  output Sum1,
  output Sum2,
  output Cout_1,
  output Cout2,
  output [3:0] out_8,
  output Cout3,
  output Cout4,
  output Sum3,
  output Sum4
);

  wire and_74ls08_1_out_9, and_74ls08_1_out_10, and_74ls08_1_out_11, and_74ls08_1_out_12, and_74ls08_2_out_9,
       and_74ls08_2_out_10, and_74ls08_2_out_11, and_74ls08_2_out_12, xor_74ls86_1_out_9,
       xor_74ls86_1_out_11, xor_74ls86_2_out_9, xor_74ls86_2_out_11;

  XOR_74LS86 xor_74ls86_1 (
    .in_5(in_2[2]), .in_7(in_3[2]), .in_1(in_2[0]), .in_3(in_3[0]), .in_6(xor_74ls86_1_out_11), .in_8(Cout2),
    .in_2(xor_74ls86_1_out_9), .in_4(in_1), .out_11(xor_74ls86_1_out_11), .out_9(xor_74ls86_1_out_9),
    .out_12(out_8[2]), .out_10(out_8[0]));
  XOR_74LS86 xor_74ls86_2 (
    .in_5(in_2[3]), .in_7(in_3[3]), .in_1(in_2[1]), .in_3(in_3[1]), .in_6(xor_74ls86_2_out_11), .in_8(Cout3),
    .in_2(xor_74ls86_2_out_9), .in_4(Cout_1), .out_11(xor_74ls86_2_out_11), .out_9(xor_74ls86_2_out_9),
    .out_12(out_8[3]), .out_10(out_8[1]));
  AND_74LS08 and_74ls08_1 (
    .in_1(in_2[0]), .in_3(in_3[0]), .in_5(in_2[2]), .in_7(in_3[2]), .in_2(xor_74ls86_1_out_9), .in_4(in_1),
    .in_6(xor_74ls86_1_out_11), .in_8(Cout2), .out_9(and_74ls08_1_out_9), .out_11(and_74ls08_1_out_11),
    .out_10(and_74ls08_1_out_10), .out_12(and_74ls08_1_out_12));
  AND_74LS08 and_74ls08_2 (
    .in_1(in_2[1]), .in_3(in_3[1]), .in_5(in_2[3]), .in_7(in_3[3]), .in_2(xor_74ls86_2_out_9), .in_4(Cout_1),
    .in_6(xor_74ls86_2_out_11), .in_8(Cout3), .out_9(and_74ls08_2_out_9), .out_11(and_74ls08_2_out_11),
    .out_10(and_74ls08_2_out_10), .out_12(and_74ls08_2_out_12));
  OR_74LS32 or_74ls32_1 (
    .in_1(and_74ls08_1_out_9), .in_3(and_74ls08_1_out_10), .in_5(and_74ls08_1_out_11),
    .in_7(and_74ls08_1_out_12), .in_2(and_74ls08_2_out_9), .in_4(and_74ls08_2_out_10),
    .in_6(and_74ls08_2_out_11), .in_8(and_74ls08_2_out_12), .out_9(Cout_1), .out_11(Cout3), .out_10(Cout2),
    .out_12(Cout4));

  assign Sum1 = out_8[0];
  assign Sum2 = out_8[1];
  assign Sum3 = out_8[2];
  assign Sum4 = out_8[3];

  // Notes on the sheet:
  //   Initial C-in
  //   always 0
  //   A
  //   B
  //   XOR
  //   <- Cout1 as Cin
  //   AND
  //   <- Cout2 as Cin3
  //   <- Cout3 as Cin4
  //   OR
endmodule

module XOR_74LS86 (
  input  in_1,
  input  in_2,
  input  in_3,
  input  in_4,
  input  in_5,
  input  in_6,
  input  in_7,
  input  in_8,
  output out_9,
  output out_10,
  output out_11,
  output out_12
);

  xor xor_1 (out_9, in_1, in_3);
  xor xor_2 (out_11, in_5, in_7);
  xor xor_3 (out_10, in_2, in_4);
  xor xor_4 (out_12, in_6, in_8);
endmodule

module AND_74LS08 (
  input  in_1,
  input  in_2,
  input  in_3,
  input  in_4,
  input  in_5,
  input  in_6,
  input  in_7,
  input  in_8,
  output out_9,
  output out_10,
  output out_11,
  output out_12
);

  and and_1 (out_9, in_1, in_3);
  and and_2 (out_11, in_5, in_7);
  and and_3 (out_10, in_2, in_4);
  and and_4 (out_12, in_6, in_8);
endmodule

module OR_74LS32 (
  input  in_1,
  input  in_2,
  input  in_3,
  input  in_4,
  input  in_5,
  input  in_6,
  input  in_7,
  input  in_8,
  output out_9,
  output out_10,
  output out_11,
  output out_12
);

  or or_1 (out_9, in_1, in_3);
  or or_2 (out_11, in_5, in_7);
  or or_3 (out_10, in_2, in_4);
  or or_4 (out_12, in_6, in_8);
endmodule

module Adder1Bit (
  input  A,
  input  B,
  input  Cin,
  output Sum,
  output Cout
);

  wire and_1_out, and_2_out, xor_1_out;

  xor xor_1 (xor_1_out, A, B);
  xor xor_2 (Sum, xor_1_out, Cin);
  and and_1 (and_1_out, xor_1_out, Cin);
  and and_2 (and_2_out, A, B);
  or or_1 (Cout, and_2_out, and_1_out);
endmodule
